# Fritzing sketch anschluss_rfid_reader (saved by Fritzing 0.9.3b)
breadboards: 1

parts:
  Microcontroller = NodeMCU V3.0
  Piezo-Buzzer = Piezo Speaker
  RFID_Reader = RFID-RC522-v2

nets:
  N1: Microcontroller.D2, Piezo-Buzzer.pin1
  N2: Microcontroller.D3, RFID_Reader.GND
  N3: Microcontroller.D4, RFID_Reader.SDA
  3V3: Microcontroller.3V3, RFID_Reader.3.3V
  N4: Microcontroller.GND#6, Microcontroller.GND#13, Microcontroller.GND#16, Microcontroller.GND#33, Piezo-Buzzer.pin2, RFID_Reader.RST
  N5: Microcontroller.D5, RFID_Reader.SCK
  N6: Microcontroller.D6, RFID_Reader.MOSI
  N7: Microcontroller.D7, RFID_Reader.MISO

custom parts:
  NodeMCU V3.0: ESP8266 based NodeMCU
  RFID-RC522-v2: A simple China made RFID-RC522 Reader; do check the pin labels, as this is a MFRC522 based clone.
